# Fritzing sketch Circuit (saved by Fritzing 0.9.2b)
breadboards: 1

parts:
  Componente1 = Arduino Ethernet Shield (Rev3)
  LCD1 = LCD screen [part_number=2]
  LED1 = LED - 5mm [color="Infrared (880nm)" package="5 mm [THT]"]
  R1 = Resistor [tolerance=±5% resistance=300 package=THT]
  R2 = Trimmer Potentiometer [maximum_resistance=10kΩ package=THT]
  T1 = LM35 Temperature Sensor [package="TO92 [THT]"]
  R3 = Resistor [tolerance=±5% resistance=10k package=THT]

nets:
  N1: Componente1.D8, LCD1.E
  N2: Componente1.PWM_D9, LCD1.RS
  GND: Componente1.GND, LCD1.VSS, LCD1.R/W, LCD1.LED-, LED1.anode, R2.leg2, T1.GND
  N3: Componente1.A0, T1.Vout
  N4: Componente1.D2, LCD1.DB7
  N5: Componente1.PWM_D3, LCD1.DB6
  N6: Componente1.PWM_D5, LCD1.DB5
  N7: Componente1.PWM_D6, LCD1.DB4
  N8: Componente1.D7, R1.Pin_1
  5V: Componente1.5V, LCD1.VDD, R2.leg1, T1.+Vs, R3.Pin_0
  N9: LCD1.V0, R2.wiper
  N10: LCD1.LED+, R3.Pin_1
  N11: LED1.cathode, R1.Pin_0
